// Logisim project tp3_4.circ as structural Verilog: 5 circuits, main circuit frequence_32btis
module frequence_32btis (
  input  [31:0] A,
  input  Load,
  output [13:0] FREQ
);

  wire CLK_out;
  wire [17:0] CMPT_q;
  wire [31:0] adder_1_out, register_1_q, register_2_q;

  Clock CLK (.out(CLK_out));
  Register #(.width(32)) register_1 (.D(A), .en(Load), .clk(CLK_out), .Q(register_1_q));  // open: clr
  Register #(.width(32)) register_2 (.D(adder_1_out), .en(1'b1), .clk(CLK_out), .Q(register_2_q), .clr(Load));
  Adder #(.width(32)) adder_1 (.a(register_1_q), .b(register_2_q), .out(adder_1_out));  // open: cin, cout
  Counter #(.max('hffffffff), .width(32)) CMPT (
    .clr(Load), .clk(CLK_out), .D(register_2_q), .Q({FREQ, CMPT_q}));  // open: load, up, count, carry
endmodule

module frequence_4bits (
  input  [3:0] A,
  input  Load,
  output [3:0] FREQ
);

  wire CLK_out;
  wire [3:0] adder_1_out, register_1_q, register_2_q;

  Clock CLK (.out(CLK_out));
  Register #(.width(4)) register_1 (.D(A), .en(Load), .clk(CLK_out), .Q(register_1_q));  // open: clr
  Register #(.width(4)) register_2 (.D(adder_1_out), .en(1'b1), .clk(CLK_out), .Q(register_2_q), .clr(Load));
  Adder #(.width(4)) adder_1 (.a(register_1_q), .b(register_2_q), .out(adder_1_out));  // open: cin, cout
  Counter #(.max('hf), .width(4)) CMPT (
    .clr(Load), .load(1'b1), .clk(CLK_out), .D(register_2_q), .Q(FREQ));  // open: up, count, carry
endmodule

module timer_16bits (
  input  [15:0] Nb_tester,
  input  Load,
  input  CLK,
  output SUP,
  output EQ
);

  wire undriven;
  wire [15:0] counter_1_q, register_1_q;

  Counter #(.max('hffff), .width(16)) counter_1 (
    .clr(Load), .clk(CLK), .Q(counter_1_q));  // open: load, up, count, D, carry
  Register #(.width(16)) register_1 (.D(Nb_tester), .en(Load), .clk(CLK), .Q(register_1_q), .clr(undriven));
  Comparator #(.width(16)) comparator_1 (.a(register_1_q), .b(counter_1_q), .gt(SUP), .eq(EQ));  // open: lt
endmodule

module timer_4bits (
  input  [3:0] Nb_teste,
  input  Load,
  output SUP,
  output EQ
);

  wire CLK_out, undriven;
  wire [3:0] counter_1_q, register_1_q;

  Clock CLK (.out(CLK_out));
  Counter #(.max('hf), .width(4)) counter_1 (
    .clr(Load), .clk(CLK_out), .Q(counter_1_q));  // open: load, up, count, D, carry
  Register #(.width(4)) register_1 (.D(Nb_teste), .en(Load), .clk(CLK_out), .Q(register_1_q), .clr(undriven));
  Comparator #(.width(4)) comparator_1 (.a(register_1_q), .b(counter_1_q), .gt(SUP), .eq(EQ));  // open: lt
endmodule

module musique (
  input  Start
);

  wire CLK_out, counter_1_carry, timer_16bits_1_eq, timer_16bits_1_sup, undriven, undriven_2;
  wire [3:0] counter_1_q;
  wire [5:0] Partition_data;
  wire [7:0] DUREE_data;
  wire [13:6] NOTE_data;

  Clock CLK (.out(CLK_out));
  Counter #(.max('hf), .width(4)) counter_1 (
    .clr(Start), .load(undriven), .up(undriven_2), .clk(CLK_out), .carry(counter_1_carry), .Q(counter_1_q));  // open: count, D
  // NoConnect on undriven
  // NoConnect on undriven_2
  // NoConnect on counter_1_carry
  ROM #(.addrWidth(4), .dataWidth(6)) Partition (.addr(counter_1_q), .data(Partition_data));
  ROM #(.addrWidth(3)) DUREE (.addr(Partition_data[2:0]), .data(DUREE_data));
  ROM #(.addrWidth(3)) NOTE (.addr(Partition_data[5:3]), .data(NOTE_data));
  timer_16bits timer_16bits_1 (
    .Nb_tester({{8{1'b0}}, DUREE_data}), .Load(1'b1), .CLK(CLK_out), .SUP(timer_16bits_1_sup),
    .EQ(timer_16bits_1_eq));
  // NoConnect on timer_16bits_1_eq
  // Buzzer #(.vol_width(1)) buzzer_1: pin names not known; wires that end beside it: {NOTE_data, {6{1'b0}}}, timer_16bits_1_sup, 1'b1

  // Notes on the sheet:
  //   contents of Partition (hex, n*v repeats v):
  //   21 e 31 31 1e 3a 25 18
  //   contents of DUREE (hex, n*v repeats v):
  //   0 1 2 3 4 5 6 7
  //   contents of NOTE (hex, n*v repeats v):
  //   0 1 2 3 4 5 6 7
endmodule
